# Fritzing sketch Ultrasonic Detector - Mark I (saved by Fritzing 0.8.7b)
breadboards: 1

parts:
  Ardunio_Mega2560_R3 = Arduino Mega 2560 (Rev3)
  HC-SR04_Ultrasonic_Sensor = SRF05 Ultrasonic Rangefinder
  R1 = Resistor [tolerance=±5% resistance=220 package=THT]
  LED1 = smd LED [color="White (4500K)" package="0603 [SMD]"]

nets:
  GND: Ardunio_Mega2560_R3.GND, HC-SR04_Ultrasonic_Sensor.GND, R1.Pin_1
  N1: Ardunio_Mega2560_R3.D13_PWM, LED1.cathode
  N2: Ardunio_Mega2560_R3.D8_PWM, HC-SR04_Ultrasonic_Sensor.Trig
  5V: Ardunio_Mega2560_R3.5V, HC-SR04_Ultrasonic_Sensor.VCC
  N3: Ardunio_Mega2560_R3.D7_PWM, HC-SR04_Ultrasonic_Sensor.Echo
  N4: R1.Pin_0, LED1.anode
